# Fritzing sketch Completo (saved by Fritzing 0.9.2b)
breadboards: 1

parts:
  Parte1 = Arduino Uno (Rev3)
  LED7 = LED - 5mm [color="Green (555nm)" package="5 mm [THT]"]
  LED8 = LED - 5mm [color="Green (555nm)" package="5 mm [THT]"]
  LED6 = LED - 5mm [color="Yellow (585nm)" package="5 mm [THT]"]
  LED5 = LED - 5mm [color="Yellow (585nm)" package="5 mm [THT]"]
  LED3 = LED - 5mm [color="Red (633nm)" package="5 mm [THT]"]
  LED1 = LED - 5mm [color="Red (633nm)" package="5 mm [THT]"]
  LED4 = LED - 5mm [color="Red (633nm)" package="5 mm [THT]"]
  R13 = Resistor [tolerance=±5% resistance=10k package=THT]
  R15 = Resistor [tolerance=±5% resistance=10k package=THT]
  R12 = Resistor [tolerance=±5% resistance=10k package=THT]
  S2 = Pushbutton [package="[THT]"]
  Parte2 = Breakout Board for Electret Microphone
  LED2 = LED - 5mm [color="Red (633nm)" package="5 mm [THT]"]
  R1 = Resistor [tolerance=±5% resistance=220 package=THT]
  R2 = Resistor [tolerance=±5% resistance=220 package=THT]
  R3 = Resistor [tolerance=±5% resistance=220 package=THT]
  R5 = Resistor [tolerance=±5% resistance=220 package=THT]
  R4 = Resistor [tolerance=±5% resistance=220 package=THT]
  R7 = Resistor [tolerance=±5% resistance=220 package=THT]
  R8 = Resistor [tolerance=±5% resistance=220 package=THT]
  R6 = Resistor [tolerance=±5% resistance=220 package=THT]
  R9 = Resistor [tolerance=±5% resistance=220 package=THT]
  R10 = Resistor [tolerance=±5% resistance=220 package=THT]
  S1 = Pushbutton [package="[THT]"]
  R14 = Resistor [tolerance=±5% resistance=10k package=THT]
  LED9 = LED - 5mm [color="Red (633nm)" package="5 mm [THT]"]
  LED10 = LED - 5mm [color="Green (555nm)" package="5 mm [THT]"]

nets:
  N1: Parte1.A0, Parte2.AUD
  N2: Parte1.D8, R3.Pin_0
  N3: Parte1.D9_PWM, R2.Pin_0
  N4: Parte1.D10_PWM/SS, R1.Pin_0
  N5: Parte1.D11_PWM/MOSI, R10.Pin_0
  N6: Parte1.D12/MISO, R9.Pin_0
  GND: Parte1.GND, LED7.cathode, LED8.cathode, LED6.cathode, LED5.cathode, LED3.cathode, LED1.cathode, LED4.cathode, R15.Pin_1, R12.Pin_0, Parte2.GND, LED2.cathode, R14.Pin_1, LED9.cathode, LED10.cathode
  N7: Parte1.AREF, R13.Pin_0, R12.Pin_1
  N8: Parte1.D1/TX, R15.Pin_0, S2.Pin_3, S2.Pin_4
  N9: Parte1.D2, S1.Pin_3, S1.Pin_4, R14.Pin_0
  N10: Parte1.D3_PWM, R8.Pin_0
  N11: Parte1.D4, R7.Pin_0
  N12: Parte1.D5_PWM, R6.Pin_0
  N13: Parte1.D6_PWM, R5.Pin_0
  N14: Parte1.D7, R4.Pin_0
  5V: Parte1.5V, R13.Pin_1, S2.Pin_1, S2.Pin_2, Parte2.VCC, S1.Pin_1, S1.Pin_2
  N15: LED7.anode, R7.Pin_1
  N16: LED8.anode, R8.Pin_1
  N17: LED6.anode, R6.Pin_1
  N18: LED5.anode, R5.Pin_1
  N19: LED3.anode, R3.Pin_1
  N20: LED1.anode, R1.Pin_1
  N21: LED4.anode, R4.Pin_1
  N22: LED2.anode, R2.Pin_1
  N23: R9.Pin_1, LED9.anode
  N24: R10.Pin_1, LED10.anode
